# Fritzing sketch Sema (saved by Fritzing 0.9.3b)
breadboards: 1

parts:
  HC-SR04_Sensor = HC-SR04 Ultrasonic Distance Sensor
  Standard_Servo_Motor = Basic Servo
  C2 = Electrolytic Capacitor [capacitance=0.47mF package="300 mil [THT, electrolytic]"]
  Voltage_Regulator_7806 = Voltage Regulator [package=to-220-alt]
  Arduino_Uno = Arduino Uno (Rev3)
  V1 = DC Power [voltage=12V]
  C1 = Electrolytic Capacitor [capacitance=0.47mF package="300 mil [THT, electrolytic]"]

nets:
  VCC: HC-SR04_Sensor.VCC, Arduino_Uno.5V
  N1: HC-SR04_Sensor.TRIG, Arduino_Uno.D9_PWM
  N2: HC-SR04_Sensor.ECHO, Arduino_Uno.GND
  N3: HC-SR04_Sensor.GND, Arduino_Uno.D10_PWM/SS
  GND: Standard_Servo_Motor.gnd, C2.-, Voltage_Regulator_7806.GND, V1.V-, C1.-
  N4: Standard_Servo_Motor.vcc, C2.+, Voltage_Regulator_7806.OUT
  N5: Standard_Servo_Motor.pulse, Arduino_Uno.D6_PWM
  N6: Voltage_Regulator_7806.IN, V1.V+, C1.+
